# Fritzing sketch chibit (saved by Fritzing 0.9.2b)
breadboards: 1

parts:
  ESP2 = ESP 12E
  LED2 = RGB LED (com. cathode, rbg) [package="5 mm [THT]"]
  R6 = Resistor [tolerance=±5% resistance=220 package="1206 [SMD]"]
  R7 = Resistor [tolerance=±5% resistance=220 package="1206 [SMD]"]
  R8 = Resistor [tolerance=±5% resistance=220 package="1206 [SMD]"]
  Part3 = LilyPad Coin Cell Battery Holder
  C2 = Ceramic Capacitor [capacitance=100nF package="100 mil [THT, multilayer]"]
  Part4 = LilyPad Button Board
  R10 = Resistor [tolerance=±5% resistance=6.8k package=THT]
  R9 = Textile Stretch Sensor [part_number=PW052]
  R11 = Resistor [tolerance=±5% resistance=6.8k package=THT]
  R12 = Resistor [tolerance=±5% resistance=6.8k package=THT]

nets:
  N1: ESP2.GPIO0, R12.Pin_1
  N2: ESP2.GPIO15, R11.Pin_1
  N3: ESP2.VCC, C2.0
  N4: ESP2.GPIO13, R6.Pin_1
  N5: ESP2.GPIO12, R7.Pin_1
  N6: ESP2.GPIO14, R8.Pin_1
  N7: ESP2.ADC, ESP2.RST, Part4.-, R10.Pin_1, R9.pin_0
  N8: LED2.red_anode, R6.Pin_0
  N9: LED2.common_cathode, Part3.+, C2.1, Part4.S, R10.Pin_0, R9.pin_1, R11.Pin_0, R12.Pin_0
  N10: LED2.blue_anode, R7.Pin_0
  N11: LED2.green_anode, R8.Pin_0

custom parts:
  ESP 12E: ESP 12e module with spi interface and wifi connection
